// Logisim project HERAprocessor356Working.circ as structural Verilog: 10 circuits, main circuit main
module main (
);

  wire clock_1_out, Control_Module_call_return, Control_Module_load_or_store, Control_Module_write;
  wire [3:0] Control_Module_input_1, Control_Module_input_2, Control_Module_write_into;
  wire [4:0] Control_Module_offset, Flags, New_Flags;
  wire [15:0] ALSU___O, B, Control_Module_write_2, Instruction, PC, R1, R2, R3, RAM___O,
       Register_Bank_output_1, rom_1_data;

  Clock clock_1 (.out(clock_1_out));
  Hex_Digit_Display hex_digit_display_1 (.value(R1[15:12]));  // open: dp
  Hex_Digit_Display hex_digit_display_2 (.value(PC[15:12]));  // open: dp
  Program_Counter_Module program_counter_module_1 (
    .New_Address(B), .Clock(clock_1_out), .Output(PC), .Flags(Flags), .Instruction(Instruction));
  Hex_Digit_Display hex_digit_display_3 (.value(R1[7:4]));  // open: dp
  Hex_Digit_Display hex_digit_display_4 (.value(R1[11:8]));  // open: dp
  Hex_Digit_Display hex_digit_display_5 (.value(PC[11:8]));  // open: dp
  Hex_Digit_Display hex_digit_display_6 (.value(PC[7:4]));  // open: dp
  Hex_Digit_Display hex_digit_display_7 (.value(R1[3:0]));  // open: dp
  Hex_Digit_Display hex_digit_display_8 (.value(PC[3:0]));  // open: dp
  ROM #(.addrWidth(16), .dataWidth(16)) rom_1 (.addr(PC), .data(rom_1_data));  // open: sel
  Hex_Digit_Display hex_digit_display_9 (.value(R2[15:12]));  // open: dp
  Hex_Digit_Display hex_digit_display_10 (.value(R2[11:8]));  // open: dp
  Hex_Digit_Display hex_digit_display_11 (.value(Instruction[15:12]));  // open: dp
  Hex_Digit_Display hex_digit_display_12 (.value(Instruction[11:8]));  // open: dp
  Hex_Digit_Display hex_digit_display_13 (.value(R2[7:4]));  // open: dp
  Hex_Digit_Display hex_digit_display_14 (.value(R2[3:0]));  // open: dp
  Hex_Digit_Display hex_digit_display_15 (.value(Instruction[7:4]));  // open: dp
  Hex_Digit_Display hex_digit_display_16 (.value(Instruction[3:0]));  // open: dp
  Control_Module Control_Module (
    .Instruction(rom_1_data), .Input_1(Control_Module_input_1), .Input_2(Control_Module_input_2),
    .Full_Instruction(Instruction), .Offset(Control_Module_offset),
    .Load_or_Store(Control_Module_load_or_store), .ALSU(ALSU___O), .Ram(RAM___O),
    .Write_2(Control_Module_write_2), .Write_Into(Control_Module_write_into), .Write(Control_Module_write),
    .PC(PC), .Call_Return(Control_Module_call_return));
  Hex_Digit_Display hex_digit_display_17 (.value(R3[15:12]));  // open: dp
  Hex_Digit_Display hex_digit_display_18 (.value(R3[11:8]));  // open: dp
  Hex_Digit_Display hex_digit_display_19 (.value(R3[7:4]));  // open: dp
  Register_Bank Register_Bank (
    .input_1(Control_Module_input_1), .Clk(clock_1_out), .input_2(Control_Module_input_2),
    .write(Control_Module_write_2), .write_into(Control_Module_write_into),
    .output_1(Register_Bank_output_1), .output_2(B), .R1(R1), .R2(R2), .R3(R3), .Wr(Control_Module_write),
    .Call_Return(Control_Module_call_return));
  Hex_Digit_Display hex_digit_display_20 (.value(R3[3:0]));  // open: dp
  RAM RAM (
    .Store_Data(Register_Bank_output_1), .Write(Control_Module_load_or_store), .Address(B),
    .Offset(Control_Module_offset), .Clock(clock_1_out), .Output(RAM___O));
  DotMatrix #(.matrixrows(1)) dotmatrix_1 (
    .col0(Flags[4]), .col1(Flags[3]), .col2(Flags[2]), .col3(Flags[1]), .col4(Flags[0]));
  Flag_bank Flag_Bank (.Clock(clock_1_out), .New_Flags(New_Flags), .Flags(Flags));
  ALSU ALSU (
    .input_1(Register_Bank_output_1), .input_2(B), .Output(ALSU___O), .Flags(Flags), .Flags_2(New_Flags),
    .Instruction(Instruction), .RAM___O(RAM___O));

  // Notes on the sheet:
  //   PC
  //   HERA processor
  //   Instruction Memory
  //   Program Code
  //   contents of rom_1 (hex, n*v repeats v):
  //   3165 3170 3961 306a 3270 396f 3178 3278
  //   Register Displays
  //   Instruction Code
  //   Flags
endmodule

module Register_Bank (
  input  [3:0] input_1,
  input  [3:0] input_2,
  input  Wr,
  input  Clk,
  input  [3:0] write_into,
  input  [15:0] write,
  input  Call_Return,
  output [15:0] output_1,
  output [15:0] output_2,
  output [15:0] R1,
  output [15:0] R2,
  output [15:0] R3
);

  wire Clk_t, decoder_3_out0, decoder_3_out1, decoder_3_out2, decoder_3_out3, decoder_3_out4, decoder_3_out5,
       decoder_3_out6, decoder_3_out7, decoder_3_out8, decoder_3_out9, decoder_3_out10, decoder_3_out11,
       decoder_3_out12, decoder_3_out13, decoder_3_out14, decoder_3_out15, r1_t, r2_t, r3_t, r4, r5, r6, r7,
       r8, r9, r10, r11, r12, r13, r14, r15;
  wire [0:0] or_2_out;
  wire [15:0] decoder_2_out0, FP_alt, FP_write, multiplexer_2_out, or_1_out, r0___O, r4___O, r5___O, r6___O,
       r7___O, r8___O, r9___O, r10___O, r11___O, r12___O, r13___O, r14___O, r15___O, register_writes,
       write_1, write_2, write_3, write_4, write_5, write_6, write_7, write_8, write_9, write_10, write_11,
       write_12, write_13, write_14, write_15;

  and and_1 (Clk_t, Wr, Clk);
  Decoder #(.select(4), .enable("false")) decoder_1 (
    .out0(register_writes[0]), .out1(register_writes[1]), .out2(register_writes[2]),
    .out3(register_writes[3]), .out4(register_writes[4]), .out5(register_writes[5]),
    .out6(register_writes[6]), .out7(register_writes[7]), .out8(register_writes[8]),
    .out9(register_writes[9]), .out10(register_writes[10]), .out11(register_writes[11]),
    .out12(register_writes[12]), .out13(register_writes[13]), .out14(register_writes[14]),
    .out15(register_writes[15]), .sel(write_into));
  Decoder #(.select(4), .enable("false")) decoder_2 (
    .out0(decoder_2_out0[0]), .out1(decoder_2_out0[1]), .out2(decoder_2_out0[2]), .out3(decoder_2_out0[3]),
    .out4(decoder_2_out0[4]), .out5(decoder_2_out0[5]), .out6(decoder_2_out0[6]), .out7(decoder_2_out0[7]),
    .out8(decoder_2_out0[8]), .out9(decoder_2_out0[9]), .out10(decoder_2_out0[10]),
    .out11(decoder_2_out0[11]), .out12(decoder_2_out0[12]), .out13(decoder_2_out0[13]),
    .out14(decoder_2_out0[14]), .out15(decoder_2_out0[15]), .sel(input_1));
  Multiplexer #(.width(16), .enable("false")) multiplexer_1 (
    .in0(write), .in1(r14___O), .out(FP_alt), .sel(Call_Return));
  assign or_1_out = 16'h4000 | decoder_2_out0;  // OR_Gate or_1, 16 bits wide
  assign {r15, r14, r13, r12, r11, r10, r9, r8, r7, r6, r5, r4, r3_t, r2_t, r1_t, or_2_out[0]} = register_writes | multiplexer_2_out;  // OR_Gate or_2, 16 bits wide
  Multiplexer #(.width(16), .enable("false")) multiplexer_2 (
    .in0({16{1'b0}}), .in1(or_1_out), .out(multiplexer_2_out), .sel(Call_Return));
  Register #(.width(16)) r0 (.Q(r0___O));  // open: D, en, clk, clr
  Register #(.width(16)) u_r4 (.D(write_4), .en(r4), .Q(r4___O), .clk(Clk_t));  // open: clr
  Register #(.width(16)) u_r8 (.D(write_8), .en(r8), .Q(r8___O), .clk(Clk_t));  // open: clr
  Register #(.width(16)) u_r12 (.D(write_12), .en(r12), .Q(r12___O), .clk(Clk_t));  // open: clr
  Register #(.width(16)) u_r1 (.D(write_1), .en(r1_t), .Q(R1), .clk(Clk_t));  // open: clr
  Register #(.width(16)) u_r5 (.D(write_5), .en(r5), .Q(r5___O), .clk(Clk_t));  // open: clr
  Register #(.width(16)) u_r9 (.D(write_9), .en(r9), .Q(r9___O), .clk(Clk_t));  // open: clr
  Register #(.width(16)) u_r13 (.D(write_13), .en(r13), .Q(r13___O), .clk(Clk_t));  // open: clr
  Decoder #(.select(4), .enable("false")) decoder_3 (
    .out0(decoder_3_out0), .out1(decoder_3_out1), .out2(decoder_3_out2), .out3(decoder_3_out3),
    .out4(decoder_3_out4), .out5(decoder_3_out5), .out6(decoder_3_out6), .out7(decoder_3_out7),
    .out8(decoder_3_out8), .out9(decoder_3_out9), .out10(decoder_3_out10), .out11(decoder_3_out11),
    .out12(decoder_3_out12), .out13(decoder_3_out13), .out14(decoder_3_out14), .out15(decoder_3_out15),
    .sel(input_1));
  Multiplexor multiplexor_1 (.ALSU_input(write), .R14(FP_alt), .Write(write_1), .FP_alt(decoder_3_out1));
  Multiplexor multiplexor_2 (.ALSU_input(write), .R14(FP_alt), .Write(write_2), .FP_alt(decoder_3_out2));
  Multiplexor multiplexor_3 (.ALSU_input(write), .R14(FP_alt), .Write(write_3), .FP_alt(decoder_3_out3));
  Multiplexor multiplexor_4 (.ALSU_input(write), .R14(FP_alt), .Write(write_4), .FP_alt(decoder_3_out4));
  Multiplexor multiplexor_5 (.ALSU_input(write), .R14(FP_alt), .Write(write_5), .FP_alt(decoder_3_out5));
  Multiplexor multiplexor_6 (.ALSU_input(write), .R14(FP_alt), .Write(write_6), .FP_alt(decoder_3_out6));
  Multiplexor multiplexor_7 (.ALSU_input(write), .R14(FP_alt), .Write(write_7), .FP_alt(decoder_3_out7));
  Multiplexor multiplexor_8 (.ALSU_input(write), .R14(FP_alt), .Write(write_8), .FP_alt(decoder_3_out8));
  Multiplexor multiplexor_9 (.ALSU_input(write), .R14(FP_alt), .Write(write_9), .FP_alt(decoder_3_out9));
  Multiplexor multiplexor_10 (.ALSU_input(write), .R14(FP_alt), .Write(write_10), .FP_alt(decoder_3_out10));
  Multiplexor multiplexor_11 (.ALSU_input(write), .R14(FP_alt), .Write(write_11), .FP_alt(decoder_3_out11));
  Multiplexor multiplexor_12 (.ALSU_input(write), .R14(FP_alt), .Write(write_12), .FP_alt(decoder_3_out12));
  Multiplexor multiplexor_13 (.ALSU_input(write), .R14(FP_alt), .Write(write_13), .FP_alt(decoder_3_out13));
  Multiplexor multiplexor_14 (.ALSU_input(write), .R14(FP_alt), .Write(write_14), .FP_alt(decoder_3_out14));
  Multiplexor multiplexor_15 (.ALSU_input(write), .R14(FP_alt), .Write(write_15), .FP_alt(decoder_3_out15));
  Multiplexer #(.width(16), .enable("false")) multiplexer_3 (
    .in0(write_14), .in1(output_1), .out(FP_write), .sel(Call_Return));
  Register #(.width(16)) u_r2 (.D(write_2), .en(r2_t), .Q(R2), .clk(Clk_t));  // open: clr
  Register #(.width(16)) u_r6 (.D(write_6), .en(r6), .Q(r6___O), .clk(Clk_t));  // open: clr
  Register #(.width(16)) u_r10 (.D(write_10), .en(r10), .Q(r10___O), .clk(Clk_t));  // open: clr
  Register #(.width(16)) u_r14 (.D(FP_write), .en(r14), .Q(r14___O), .clk(Clk_t));  // open: clr
  Register #(.width(16)) u_r3 (.D(write_3), .en(r3_t), .Q(R3), .clk(Clk_t));  // open: clr
  Register #(.width(16)) u_r7 (.D(write_7), .en(r7), .Q(r7___O), .clk(Clk_t));  // open: clr
  Register #(.width(16)) u_r11 (.D(write_11), .en(r11), .Q(r11___O), .clk(Clk_t));  // open: clr
  Register #(.width(16)) u_r15 (.D(write_15), .en(r15), .Q(r15___O), .clk(Clk_t));  // open: clr
  Multiplexer #(.select(4), .width(16), .enable("false")) multiplexer_4 (
    .in0(r0___O), .in1(R1), .in2(R2), .in3(R3), .in4(r4___O), .in5(r5___O), .in6(r6___O), .in7(r7___O),
    .in8(r8___O), .in9(r9___O), .in10(r10___O), .in11(r11___O), .in12(r12___O), .in13(r13___O),
    .in14(r14___O), .in15(r15___O), .out(output_1), .sel(input_1));
  Multiplexer #(.select(4), .width(16), .enable("false")) multiplexer_5 (
    .in0(r0___O), .in1(R1), .in2(R2), .in3(R3), .in4(r4___O), .in5(r5___O), .in6(r6___O), .in7(r7___O),
    .in8(r8___O), .in9(r9___O), .in10(r10___O), .in11(r11___O), .in12(r12___O), .in13(r13___O),
    .in14(r14___O), .in15(r15___O), .out(output_2), .sel(input_2));

  // Other names for the same wires on the sheet: C_R = Call_Return; New_FP[15:0] = output_1; r1___O[15:0] = R1;
  //   r2___O[15:0] = R2; r3___O[15:0] = R3

  // Notes on the sheet:
  //   Only updates the registers if write is activated
  //   FP_alt only differs from write when the instruction is Call or Return
  //   when it becomes the val currenlty in r14 (the FP register)
  //   Call and return logic is below
  //   This is the logic for determining which registers can be written to
  //   It's usually just one register, but during Call and Return
  //   r14 and one other register are also written to
  //   Call and return
  //   The skinny modules are multiplexors
  //   One register gets FP_alt instead of write as its input
endmodule

module Flag_bank (
  input  Clock,
  input  [4:0] New_Flags,
  output [4:0] Flags
);

  D_Flip_Flop F0___Sign (.clk(Clock), .D(New_Flags[0]), .Q(Flags[0]));  // open: Qn, preset, en, reset
  D_Flip_Flop F1___Zero (.clk(Clock), .D(New_Flags[1]), .Q(Flags[1]));  // open: Qn, preset, en, reset
  D_Flip_Flop F2___Overflow (.clk(Clock), .D(New_Flags[2]), .Q(Flags[2]));  // open: Qn, preset, en, reset
  D_Flip_Flop F3___Carry (.clk(Clock), .D(New_Flags[3]), .Q(Flags[3]));  // open: Qn, preset, en, reset
  D_Flip_Flop F4___Carry_Block (.clk(Clock), .D(New_Flags[4]), .Q(Flags[4]));  // open: Qn, preset, en, reset

  // Other names for the same wires on the sheet: Clk = Clock
endmodule

module ALSU (
  input  [15:0] input_1,
  input  [15:0] input_2,
  input  [4:0] Flags,
  input  [15:0] Instruction,
  input  [15:0] RAM___O,
  output [15:0] Output,
  output [4:0] Flags_2
);

  wire _3_Carry, _3_Overflow, and_6_out, and_7_out, and_8_out, Carry___Add, Carry___Mul, Carry___Sub,
       Carry_in___Add, Carry_in___Sub, nor_1_out, not_2_out, Overflow___Add, Overflow___Mul, Overflow___Sub,
       subtractor_1_bout, xnor_1_out, xnor_2_out, xnor_3_out, xor_2_out, xor_3_out, xor_4_out;
  wire [3:1] _3_Flags;
  wire [4:0] Flag_Setting;
  wire [5:0] Inc_Dec;
  wire [15:0] _3___O, Add___O, And___O, Mul_0___16, Mul___Carry_Check, Mul___O, Or___O, SetLo___O, Sub___O,
       Xor___O;

  and and_1 (Carry_in___Add, Flags[3], ~Flags[4]);  // AND_Gate
  and and_2 (Carry_in___Sub, ~Flags[4], ~Flags[3]);  // AND_Gate
  assign And___O = input_1 & input_2;  // AND_Gate and_3, 16 bits wide
  assign Or___O = input_1 | input_2;  // OR_Gate or_1, 16 bits wide
  assign Xor___O = input_1 ^ input_2;  // XOR_Gate xor_1, 16 bits wide
  Adder #(.width(16)) adder_1 (.a(input_1), .b(input_2), .out(Add___O), .cin(Carry_in___Add), .cout(Carry___Add));
  xnor xnor_1 (xnor_1_out, input_1[15], input_2[15]);
  xor xor_2 (xor_2_out, input_2[15], Add___O[15]);
  Subtractor #(.width(16)) subtractor_1 (
    .a(input_1), .b(input_2), .out(Sub___O), .bin(Carry_in___Sub), .bout(subtractor_1_bout));
  not not_1 (Carry___Sub, subtractor_1_bout);
  xor xor_3 (xor_3_out, input_1[15], input_2[15]);
  xnor xnor_2 (xnor_2_out, input_2[15], Sub___O[15]);
  Multiplier #(.width(16)) multiplier_1 (
    .a(input_1), .b(input_2), .out(Mul_0___16), .cout(Mul___Carry_Check));  // open: cin
  Comparator #(.width(16), .mode("unsigned")) comparator_1 (
    .a(Mul___Carry_Check), .b({16{1'b0}}), .gt(Carry___Mul));  // open: eq, lt
  xor xor_4 (xor_4_out, input_1[15], input_2[15]);
  not not_2 (not_2_out, Mul_0___16[15]);
  xnor xnor_3 (xnor_3_out, input_1[15], input_2[15]);
  and and_4 (Overflow___Add, xnor_1_out, xor_2_out);
  and and_5 (Overflow___Sub, xor_3_out, xnor_2_out);
  Multiplexer #(.width(16), .enable("false")) multiplexer_1 (
    .in0(Mul_0___16), .in1(Mul___Carry_Check), .out(Mul___O), .sel(and_6_out));
  and and_6 (and_6_out, ~Flags[4], nor_1_out, Flags[0]);  // AND_Gate
  nor nor_1 (nor_1_out, Flags[3], Flags[2], Flags[1]);
  and and_7 (and_7_out, xor_4_out, not_2_out);
  and and_8 (and_8_out, xnor_3_out, Mul_0___16[15]);
  or or_2 (Overflow___Mul, and_7_out, and_8_out);
  assign SetLo___O = {{8{Instruction[7]}}, Instruction[7:0]};  // Bit_Extender bit_extender_1
  Opcode_3 Opcode_3 (
    .input_1(input_1), .input_2(input_2), .Flags(Flags), .New_Flags({Instruction[8], Instruction[3:0]}),
    .Flag_Ops(Instruction[11:10]), .Inc_Dec_Input(Inc_Dec), ._8_11(Instruction[7:4]),
    .Shift_Codes(Instruction[7:4]), .Save_or_Restore(Instruction[3]), .Output(_3___O),
    .Flag_Output(Flag_Setting), ._3_Overflow(_3_Overflow), ._3_Flags({Flags[4], _3_Flags, Output[15]}),
    ._3_Carry(_3_Carry));
  Comparator #(.width(16)) comparator_2 (.a({16{1'b0}}), .b(Output), .eq(_3_Flags[1]));  // open: gt, lt
  Multiplexer #(.select(4), .enable("false")) multiplexer_2 (
    .in0(Flags[3]), .in1(Flags[3]), .in2(Flags[3]), .in3(_3_Carry), .in4(Flags[3]), .in5(Flags[3]),
    .in6(Flags[3]), .in7(Flags[3]), .in8(Flags[3]), .in9(Flags[3]), .in10(Carry___Add), .in11(Carry___Sub),
    .in12(Carry___Mul), .in13(Flags[3]), .in14(Flags[3]), .in15(Flags[3]), .out(_3_Flags[3]),
    .sel(Instruction[15:12]));
  Multiplexer #(.select(4), .enable("false")) multiplexer_3 (
    .in0(Flags[2]), .in1(Flags[2]), .in2(Flags[2]), .in3(_3_Overflow), .in4(Flags[2]), .in5(Flags[2]),
    .in6(Flags[2]), .in7(Flags[2]), .in8(Flags[2]), .in9(Flags[2]), .in10(Overflow___Add),
    .in11(Overflow___Sub), .in12(Overflow___Mul), .in13(Flags[2]), .in14(Flags[2]), .in15(Flags[2]),
    .out(_3_Flags[2]), .sel(Instruction[15:12]));
  Multiplexer #(.select(4), .width(16), .enable("false")) multiplexer_4 (
    .in3(_3___O), .in4(RAM___O), .in5(RAM___O), .in8(And___O), .in9(Or___O), .in10(Add___O), .in11(Sub___O),
    .in12(Mul___O), .in13(Xor___O), .in14(SetLo___O), .in15({Instruction[7:0], input_1[7:0]}), .out(Output),
    .sel(Instruction[15:12]));  // open: in0, in1, in2, in6, in7
  Multiplexer #(.select(4), .width(5), .enable("false")) multiplexer_5 (
    .in0(Flags), .in1(Flags), .in2({Flags[4], _3_Flags, Output[15]}), .in3(Flag_Setting),
    .in4({Flags[4], _3_Flags, Output[15]}), .in5({Flags[4], _3_Flags, Output[15]}), .in6(Flags), .in7(Flags),
    .in8({Flags[4], _3_Flags, Output[15]}), .in9({Flags[4], _3_Flags, Output[15]}),
    .in10({Flags[4], _3_Flags, Output[15]}), .in11({Flags[4], _3_Flags, Output[15]}),
    .in12({Flags[4], _3_Flags, Output[15]}), .in13({Flags[4], _3_Flags, Output[15]}), .in14(Flags),
    .in15(Flags), .out(Flags_2), .sel(Instruction[15:12]));

  // Other names for the same wires on the sheet: _3_Flags (some bits) = {Flags[4], Output[15]}; Sign = Output[15];
  //   Zero_Negative_Flags[15:0] = Output; Zero = _3_Flags[1]; Overflow = _3_Flags[2]; Carry = _3_Flags[3];
  //   Cur_Flags[4:0] = Flags; _8_11[3:0] = Instruction[11:8]; Flag_Ops[1:0] = Instruction[11:10];
  //   Instruction_t[3:0] = Instruction[15:12]; New_Flags[4:0] = {Instruction[8], Instruction[3:0]};
  //   RAM[15:0] = RAM___O; SetHigh___O[15:0] = {Instruction[7:0], input_1[7:0]}; _0_3[3:0] = Instruction[3:0];
  //   Inc_Dec_t[5:0] = Instruction[5:0]; New_Set[7:0] = Instruction[7:0]; R_S = Instruction[3];
  //   _4_7[3:0] = Instruction[7:4]; Shift_Chooser[3:0] = Instruction[7:4]

  // Notes on the sheet:
  //   Logical Operations
  //   And
  //   Or
  //   Xor
  //   Arithmetic
  //   Add
  //   Overflow Logic for Add
  //   Sub
  //   Overflow Logic for Sub
  //   Mul
  //   Carry Logic for Mul
  //   Overflow Logic for Mul
  //   Direct Assignment
  //   Set Low
  //   Set High
  //   Opcode 3
  //   Flag Logic
  //   Carry Flag
  //   Overflow Flag
  //   Flag Output
  //   Output
endmodule

module Control_Module (
  input  [15:0] Instruction,
  input  [15:0] PC,
  input  [15:0] Ram,
  input  [15:0] ALSU,
  output [15:0] Full_Instruction,
  output [3:0] Input_1,
  output Write,
  output [4:0] Offset,
  output Load_or_Store,
  output Call_Return,
  output [3:0] Input_2,
  output [15:0] Write_2,
  output [3:0] Write_Into
);

  wire and_1_out, comparator_1_eq, not_1_out, not_2_out;
  wire [15:0] adder_1_out;

  assign Load_or_Store = and_1_out ? Instruction[13] : 1'bz;  // Controlled_Buffer controlled_buffer_1
  and and_1 (and_1_out, not_1_out, Instruction[14]);
  not not_1 (not_1_out, Instruction[15]);
  Adder #(.width(16)) adder_1 (.a(PC), .b(16'h1), .out(adder_1_out));  // open: cin, cout
  Multiplexer #(.select(4), .width(16), .enable("false")) multiplexer_1 (
    .in0(ALSU), .in1(ALSU), .in2(adder_1_out), .in3(ALSU), .in4(Ram), .in5(Ram), .in6(Ram), .in7(Ram),
    .in8(ALSU), .in9(ALSU), .in10(ALSU), .in11(ALSU), .in12(ALSU), .in13(ALSU), .in14(ALSU), .in15(ALSU),
    .out(Write_2), .sel(Instruction[15:12]));
  Multiplexer #(.select(4), .width(4), .enable("false")) multiplexer_2 (
    .in0(Instruction[7:4]), .in1(Instruction[7:4]), .in2(Instruction[7:4]), .in3(Instruction[11:8]),
    .in4(Instruction[7:4]), .in5(Instruction[7:4]), .in6(Instruction[11:8]), .in7(Instruction[11:8]),
    .in8(Instruction[7:4]), .in9(Instruction[7:4]), .in10(Instruction[7:4]), .in11(Instruction[7:4]),
    .in12(Instruction[7:4]), .in13(Instruction[7:4]), .in14(Instruction[7:4]), .in15(Instruction[11:8]),
    .out(Input_1), .sel(Instruction[15:12]));
  Multiplexer #(.select(4), .width(4), .enable("false")) multiplexer_3 (
    .in0(Instruction[3:0]), .in1(Instruction[3:0]), .in2(Instruction[3:0]), .in3(Instruction[3:0]),
    .in4(Instruction[3:0]), .in5(Instruction[3:0]), .in6(Instruction[3:0]), .in7(Instruction[3:0]),
    .in8(Instruction[3:0]), .in9(Instruction[3:0]), .in10(Instruction[3:0]), .in11(Instruction[3:0]),
    .in12(Instruction[3:0]), .in13(Instruction[3:0]), .in14(Instruction[3:0]), .in15(Instruction[3:0]),
    .out(Input_2), .sel(Instruction[15:12]));
  not not_2 (not_2_out, comparator_1_eq);
  Comparator #(.width(4), .mode("unsigned")) comparator_1 (
    .a(Instruction[15:12]), .b(4'b0010), .eq(comparator_1_eq));  // open: gt, lt
  assign Write_Into = not_2_out ? Instruction[11:8] : 4'bz;  // Controlled_Buffer controlled_buffer_2
  assign Write_Into = comparator_1_eq ? Instruction[3:0] : 4'bz;  // Controlled_Buffer controlled_buffer_3
  Multiplexer #(.select(4), .enable("false")) multiplexer_4 (
    .in0(1'b0), .in1(1'b0), .in2(1'b1), .in3(1'b1), .in4(1'b1), .in5(1'b1), .in6(1'b0), .in7(1'b0),
    .in8(1'b1), .in9(1'b1), .in10(1'b1), .in11(1'b1), .in12(1'b1), .in13(1'b1), .in14(1'b1), .in15(1'b1),
    .out(Write), .sel(Instruction[15:12]));
  Comparator #(.width(4), .mode("unsigned")) comparator_2 (
    .a(Instruction[15:12]), .b(4'b0010), .eq(Call_Return));  // open: gt, lt

  assign Full_Instruction = Instruction;
  assign Offset = {Instruction[12], Instruction[7:4]};

  // Other names for the same wires on the sheet: B[3:0] = Instruction[3:0]; D[3:0] = Instruction[11:8];
  //   Instruction_t[3:0] = Instruction[15:12]; A[3:0] = Instruction[7:4]

  // Notes on the sheet:
  //   For Load and Store
  //   Choose which writes to register
  //   input 1
  //   input 2
  //   Whether or not instruction updates registers
endmodule

module Opcode_3 (
  input  [15:0] input_1,
  input  [15:0] input_2,
  input  [4:0] Flags,
  input  [4:0] New_Flags,
  input  [1:0] Flag_Ops,
  input  [5:0] Inc_Dec_Input,
  input  [3:0] _8_11,
  input  Save_or_Restore,
  input  [3:0] Shift_Codes,
  input  [4:0] _3_Flags,
  output [15:0] Output,
  output [4:0] Flag_Output,
  output _3_Overflow,
  output _3_Carry
);

  wire ASL_Overflow, Carry___Add, Carry___Dec, Carry___Inc, Inc_Dec_Carry, Inc_Dec_Overflow, Overflow___Dec,
       Overflow___Inc, Shift_Carry, Shift_Overflow, subtractor_1_bout, xnor_1_out, xnor_2_out, xnor_3_out,
       xor_1_out, xor_2_out, xor_3_out;
  wire [4:0] FOFF, FON, FON_FOFF, multiplexer_7_out;
  wire [15:0] ASL___O, ASR___O, Dec___O, Inc___O, Inc_Dec_Extended, LSL___O, LSR___O, multiplexer_6_out,
       SAVEF___O, Shift_Add___O;

  assign Inc_Dec_Extended = {{10{1'b0}}, Inc_Dec_Input};  // Bit_Extender bit_extender_1
  Shifter #(.width(16)) shifter_1 (.in(input_2), .\dist (4'b0001), .out(LSL___O));
  Shifter #(.width(16), .shift("lr")) shifter_2 (.in(input_2), .\dist (4'b0001), .out(LSR___O));
  Shifter #(.width(16)) shifter_3 (.in(input_2), .\dist (4'b0001), .out(ASL___O));
  Shifter #(.width(16), .shift("ar")) shifter_4 (.in(input_2), .\dist (4'b0001), .out(ASR___O));
  Adder #(.width(16)) adder_1 (.a(input_2), .b(input_2), .out(Shift_Add___O), .cout(Carry___Add));  // open: cin
  xnor xnor_1 (xnor_1_out, input_2[15], input_2[15]);
  xor xor_1 (xor_1_out, input_2[15], Shift_Add___O[15]);
  and and_1 (ASL_Overflow, xnor_1_out, xor_1_out);
  Multiplexer #(.select(3), .enable("false")) multiplexer_1 (
    .in0(1'b0), .in1(1'b0), .in2(1'b0), .in3(1'b0), .in4(ASL_Overflow), .in5(1'b0), .in6(1'b0), .in7(1'b0),
    .out(Shift_Overflow), .sel(_8_11[2:0]));
  Multiplexer #(.select(3), .enable("false")) multiplexer_2 (
    .in0(input_2[15]), .in1(input_2[0]), .in2(input_2[15]), .in3(input_2[0]), .in4(input_2[15]),
    .in5(input_2[0]), .out(Shift_Carry), .sel(_8_11[2:0]));  // open: in6, in7
  assign FON = Flags | New_Flags;  // OR_Gate or_1, 5 bits wide
  assign FOFF = Flags & ~New_Flags;  // AND_Gate and_2, 5 bits wide
  Multiplexer #(.select(2), .width(5), .enable("false")) multiplexer_3 (
    .in0(FON), .in1(New_Flags), .in2(FOFF), .in3({Flags[4], New_Flags[3:0]}), .out(FON_FOFF), .sel(Flag_Ops));
  assign SAVEF___O = {{11{1'b0}}, Flags};  // Bit_Extender bit_extender_2
  Adder #(.width(16)) adder_2 (.a(input_1), .b(Inc_Dec_Extended), .out(Inc___O), .cin(1'b1), .cout(Carry___Inc));
  Subtractor #(.width(16)) subtractor_1 (
    .a(input_1), .b(Inc_Dec_Extended), .out(Dec___O), .bin(1'b1), .bout(subtractor_1_bout));
  Multiplexer #(.enable("false")) multiplexer_4 (
    .in0(Overflow___Inc), .in1(Overflow___Dec), .out(Inc_Dec_Overflow), .sel(_8_11[2]));
  Multiplexer #(.enable("false")) multiplexer_5 (
    .in0(Carry___Inc), .in1(Carry___Dec), .out(Inc_Dec_Carry), .sel(_8_11[2]));
  xnor xnor_2 (xnor_2_out, input_1[15], Inc_Dec_Extended[15]);
  xor xor_2 (xor_2_out, Inc_Dec_Extended[15], Inc___O[15]);
  not not_1 (Carry___Dec, subtractor_1_bout);
  xor xor_3 (xor_3_out, input_1[15], Inc_Dec_Extended[15]);
  xnor xnor_3 (xnor_3_out, Inc_Dec_Extended[15], Dec___O[15]);
  and and_3 (Overflow___Inc, xnor_2_out, xor_2_out);
  and and_4 (Overflow___Dec, xor_3_out, xnor_3_out);
  Multiplexer #(.width(16), .enable("false")) multiplexer_6 (
    .in0(SAVEF___O), .in1(input_1), .out(multiplexer_6_out), .sel(Save_or_Restore));
  Multiplexer #(.width(5), .enable("false")) multiplexer_7 (
    .in0(Flags), .in1(input_1[4:0]), .out(multiplexer_7_out), .sel(Save_or_Restore));
  Multiplexer #(.select(4), .width(16), .enable("false")) multiplexer_8 (
    .in0(LSL___O), .in1(LSR___O), .in4(ASL___O), .in5(ASR___O), .in7(multiplexer_6_out), .in8(Inc___O),
    .in9(Inc___O), .in10(Inc___O), .in11(Inc___O), .in12(Dec___O), .in13(Dec___O), .in14(Dec___O),
    .in15(Dec___O), .out(Output), .sel(Shift_Codes));  // open: in2, in3, in6
  Multiplexer #(.select(4), .width(5), .enable("false")) multiplexer_9 (
    .in0(_3_Flags), .in1(_3_Flags), .in4(_3_Flags), .in5(_3_Flags), .in6(FON_FOFF), .in7(multiplexer_7_out),
    .in8(_3_Flags), .in9(_3_Flags), .in10(_3_Flags), .in11(_3_Flags), .in12(_3_Flags), .in13(_3_Flags),
    .in14(_3_Flags), .in15(_3_Flags), .out(Flag_Output), .sel(Shift_Codes));  // open: in2, in3
  Multiplexer #(.enable("false")) multiplexer_10 (
    .in0(Shift_Overflow), .in1(Inc_Dec_Overflow), .out(_3_Overflow), .sel(_8_11[3]));
  Multiplexer #(.enable("false")) multiplexer_11 (
    .in0(Shift_Carry), .in1(Inc_Dec_Carry), .out(_3_Carry), .sel(_8_11[3]));

  // Other names for the same wires on the sheet: _4_7[3:0] = _8_11; Cur_Flags[4:0] = Flags;
  //   FSET4[4:0] = {Flags[4], New_Flags[3:0]}; FSET5[4:0] = New_Flags; R_S = Save_or_Restore;
  //   Shift_Chooser[3:0] = Shift_Codes

  // Notes on the sheet:
  //   Shift by
  //   Shift by
  //   Shift by
  //   Shift by
  //   Shift
  //   LSL
  //   LSR
  //   ASL
  //   ASR
  //   Shift Overflow and Carry Logic
  //   Flag Setting
  //   FON
  //   FOFF
  //   FSET5
  //   FSET4
  //   SAVEF
  //   Increment and Decrement
  //   Increment
  //   Overflow Logic for Inc
  //   Decrement
  //   Overflow Logic for Dec
  //   Choose output and flags
  //   Chooses which output when opcode = 3
  //   S&F Flag Chooser
endmodule

module RAM (
  input  [15:0] Store_Data,
  input  Write,
  input  [15:0] Address,
  input  [4:0] Offset,
  input  Clock,
  output [15:0] Output
);

  wire not_1_out;
  wire [15:0] adder_1_out, bit_extender_1_out;

  assign bit_extender_1_out = {{11{1'b0}}, Offset};  // Bit_Extender bit_extender_1
  assign Output = Write ? Store_Data : 16'bz;  // Controlled_Buffer controlled_buffer_1
  Adder #(.width(16)) adder_1 (.a(Address), .b(bit_extender_1_out), .out(adder_1_out));  // open: cin, cout
  not not_1 (not_1_out, Write);
  RAM_part #(.addrWidth(16), .dataWidth(16)) ram_1 (
    .addr(adder_1_out), .data(Output), .clk(Clock), .ld(not_1_out));  // open: sel, clr

  // Other names for the same wires on the sheet: Clk = Clock

  // Notes on the sheet:
  //   This is a buffer, so data will only be sent from Store Data if Write is true
  //   RAM can read and send data from the same point (D)
endmodule

module Program_Counter_Module (
  input  [4:0] Flags,
  input  [15:0] New_Address,
  input  Clock,
  input  [15:0] Instruction,
  output [15:0] Output
);

  wire and_1_out, Branch_Logic_write, comparator_1_gt, not_1_out, or_1_out;
  wire [15:0] adder_1_out, bit_extender_1_out, multiplexer_1_out;

  assign bit_extender_1_out = {{8{Instruction[7]}}, Instruction[7:0]};  // Bit_Extender bit_extender_1
  Adder #(.width(16)) adder_1 (.a(Output), .b(bit_extender_1_out), .out(adder_1_out));  // open: cin, cout
  or or_1 (or_1_out, Instruction[12], Instruction[13]);
  Multiplexer #(.width(16), .enable("false")) multiplexer_1 (
    .in0(adder_1_out), .in1(New_Address), .out(multiplexer_1_out), .sel(or_1_out));
  Comparator #(.width(4), .mode("unsigned")) comparator_1 (
    .a(4'b0011), .b(Instruction[15:12]), .gt(comparator_1_gt));  // open: eq, lt
  and and_1 (and_1_out, comparator_1_gt, Branch_Logic_write);
  Branch_Logic Branch_Logic (.Type(Instruction[11:8]), .Flags(Flags), .Write(Branch_Logic_write));
  Counter #(.width(16), .max('hffff)) counter_1 (
    .load(and_1_out), .D(multiplexer_1_out), .count(not_1_out), .Q(Output), .clk(Clock));  // open: carry, clr
  not not_1 (not_1_out, and_1_out);

  // Other names for the same wires on the sheet: Cur_Address[15:0] = Output; Relative[7:0] = Instruction[7:0];
  //   Type[3:0] = Instruction[11:8]; Instruct[3:0] = Instruction[15:12]
endmodule

module Branch_Logic (
  input  [3:0] Type,
  input  [4:0] Flags,
  output Write
);

  wire BG, BGE, BL, BLE, BUG, BULE, not_4_out, not_5_out, not_6_out, not_7_out;

  xor xor_1 (BL, Flags[0], Flags[2]);
  or or_1 (BLE, BL, Flags[1]);
  or or_2 (BULE, ~Flags[3], Flags[1]);  // OR_Gate
  not not_1 (BGE, BL);
  not not_2 (BG, BLE);
  not not_3 (BUG, BULE);
  not not_4 (not_4_out, Flags[1]);
  not not_5 (not_5_out, Flags[3]);
  not not_6 (not_6_out, Flags[0]);
  not not_7 (not_7_out, Flags[2]);
  Multiplexer #(.select(4), .enable("false")) multiplexer_1 (
    .in0(1'b1), .in1(1'b1), .in2(BL), .in3(BGE), .in4(BLE), .in5(BG), .in6(BULE), .in7(BUG), .in8(Flags[1]),
    .in9(not_4_out), .in10(Flags[3]), .in11(not_5_out), .in12(Flags[0]), .in13(not_6_out), .in14(Flags[2]),
    .in15(not_7_out), .out(Write), .sel(Type));

  // Other names for the same wires on the sheet: S = Flags[0]; Z = Flags[1]; V = Flags[2]; C = Flags[3];
  //   CBON = Flags[4]

  // Notes on the sheet:
  //   Greater and Less than (Signed)
  //   Greater and Less than (Unsigned)
endmodule

module Multiplexor (
  input  [15:0] ALSU_input,
  input  [15:0] R14,
  input  FP_alt,
  output [15:0] Write
);

  Multiplexer #(.width(16), .enable("false")) multiplexer_1 (.in0(ALSU_input), .in1(R14), .out(Write), .sel(FP_alt));

  // Notes on the sheet:
  //   Multiplexor module used in Register Bank
endmodule
